# Fritzing sketch Diagrama (saved by Fritzing 0.9.3b)
breadboards: 2

parts:
  LCM1602_IIC1 = LCM1602 IIC [part_number="LCM1602 IIC" chip_label="LCM1602 IIC" package="DIP (Dual Inline) [THT]"]
  LCD1 = LCD screen
  Componente1 = Arduino Uno (Rev3)
  R1 = Resistor [tolerance=±5% resistance=10k package="0402 [SMD]"]
  U1 = QRD1114 [package=qrd1114]
  SW1 = DIP Switch 8 Position [package=dipswitch-08]
  R3 = Resistor [tolerance=±5% resistance=470 package="0402 [SMD]"]
  R4 = Resistor [tolerance=±5% resistance=470 package="0402 [SMD]"]
  R5 = Resistor [tolerance=±5% resistance=470 package="0402 [SMD]"]
  R6 = Resistor [tolerance=±5% resistance=470 package="0402 [SMD]"]
  LED1 = smd LED [color="Red (633nm)" package="0805 [SMD]"]
  LED2 = smd LED [color="Green (555nm)" package="0805 [SMD]"]
  R7 = Resistor [tolerance=±5% resistance=330 package="0402 [SMD]"]
  R8 = Resistor [tolerance=±5% resistance=330 package="0402 [SMD]"]
  SP1 = SPEAKER [package=pcb_mount_speaker]
  LED3 = smd LED [color="White (8000K)" package="0805 [SMD]"]
  R2 = Resistor [tolerance=±5% resistance=330 package="0402 [SMD]"]
  R9 = Resistor [tolerance=±5% resistance=330 package="0402 [SMD]"]
  Q1 = NPN-Transistor [package="TO92 [THT]"]
  U2 = POT [package=pot_alpha_rv16af-20]
  R11 = Resistor [tolerance=±5% resistance=1k package="0402 [SMD]"]
  R12 = Photocell (LDR) [package=THT]
  R13 = Resistor [tolerance=±5% resistance=100 package="0402 [SMD]"]
  VCC1 = Battery block 9V

nets:
  VSS: LCM1602_IIC1.VSS, LCD1.VSS
  VDD: LCM1602_IIC1.VDD, LCD1.VDD
  N1: LCM1602_IIC1.V0, LCD1.V0
  N2: LCM1602_IIC1.RS, LCD1.RS
  N3: LCM1602_IIC1.RW, LCD1.R/W
  N4: LCM1602_IIC1.E, LCD1.E
  N5: LCM1602_IIC1.D0, LCD1.DB0
  N6: LCM1602_IIC1.D1, LCD1.DB1
  N7: LCM1602_IIC1.D2, LCD1.DB2
  N8: LCM1602_IIC1.D3, LCD1.DB3
  N9: LCM1602_IIC1.D4, LCD1.DB4
  N10: LCM1602_IIC1.D5, LCD1.DB5
  N11: LCM1602_IIC1.D6, LCD1.DB6
  N12: LCM1602_IIC1.D7, LCD1.DB7
  N13: LCM1602_IIC1.A, LCD1.LED+
  N14: LCM1602_IIC1.K, LCD1.LED-
  GND: LCM1602_IIC1.GND, Componente1.GND, U1.E, R3.Pin_1, R4.Pin_1, R5.Pin_1, R6.Pin_1, R7.Pin_1, R8.Pin_1, SP1.+, R2.Pin_1, R9.Pin_1, R12.pin_0, VCC1.-
  VCC: LCM1602_IIC1.VCC, LCM1602_IIC1.SDA, LCM1602_IIC1.SCL, Componente1.A4/SDA, Componente1.A5/SCL, Componente1.5V, R1.Pin_0, U1.A, SW1.1, SW1.2, SW1.3, SW1.4
  N15: LCM1602_IIC1.LED_A, LCM1602_IIC1.LED_B
  N16: Componente1.D8, R13.Pin_0
  N17: Componente1.D10_PWM/SS, LED2.anode
  N18: Componente1.D11_PWM/MOSI, LED1.anode
  N19: Componente1.D12/MISO, LED3.anode, Q1.C
  N20: Componente1.D2, R1.Pin_1, U1.C
  N21: Componente1.D3_PWM, SW1.13, R6.Pin_0
  N22: Componente1.D4, SW1.14, R5.Pin_0
  N23: Componente1.D5_PWM, SW1.15, R4.Pin_0
  N24: Componente1.D6_PWM, SW1.16, R3.Pin_0
  N25: U1.K, R2.Pin_0
  N26: LED1.cathode, R7.Pin_0
  N27: LED2.cathode, R8.Pin_0
  N28: SP1.-, R13.Pin_1
  N29: LED3.cathode, R9.Pin_0
  N30: Q1.E, U2.S, VCC1.+
  N31: Q1.B, R11.Pin_1, R12.pin_1
  N32: U2.A, R11.Pin_0

custom parts:
  LCM1602 IIC: I2C-Module to use a 1602 or 2004 LCD on with the wire.h libory Serial LCD Modul
